# Fritzing sketch SnakeSchema (saved by Fritzing 0.9.1b)
breadboards: 2

parts:
  Part1 = Arduino Uno (Rev3)
  R1 = Resistor [tolerance=±5% resistance=220 package=THT]
  R2 = Resistor [tolerance=±5% resistance=220 package=THT]
  R3 = Resistor [tolerance=±5% resistance=220 package=THT]
  R4 = Resistor [tolerance=±5% resistance=220 package=THT]
  R5 = Resistor [tolerance=±5% resistance=220 package=THT]
  R6 = Resistor [tolerance=±5% resistance=220 package=THT]
  R7 = Resistor [tolerance=±5% resistance=220 package=THT]
  R8 = Resistor [tolerance=±5% resistance=220 package=THT]
  Disp3 = LBT2088AH [part_number=LBT2088AH]

nets:
  N1: Part1.A0, R8.Pin_0
  N2: Part1.A1, R7.Pin_0
  N3: Part1.A2, R6.Pin_0
  N4: Part1.A3, R5.Pin_0
  N5: Part1.A4/SDA, R4.Pin_0
  N6: Part1.A5/SCL, R3.Pin_0
  N7: Part1.D8, Disp3.pin_7
  N8: Part1.D9_PWM, Disp3.pin_8
  N9: Part1.D11_PWM/MOSI, R1.Pin_0
  N10: Part1.D12/MISO, R2.Pin_0
  N11: Part1.D2, Disp3.pin_5
  N12: Part1.D3_PWM, Disp3.pin_11
  N13: Part1.D4, Disp3.pin_12
  N14: Part1.D5_PWM, Disp3.pin2
  N15: Part1.D6_PWM, Disp3.pin_14
  N16: Part1.D7, Disp3.pin_3
  N17: R2.Pin_1, Disp3.pin_6
  N18: R3.Pin_1, Disp3.pin_13
  N19: R4.Pin_1, Disp3.pin_10
  N20: R5.Pin_1, Disp3.pin_15
  N21: R6.Pin_1, Disp3.pin_9
  N22: R7.Pin_1, Disp3.pin_4
  N23: R8.Pin_1, Disp3.pin_16

custom parts:
  LBT2088AH: LED Matrix Display 8x8 red 60.5mm
